# Fritzing sketch DataProducer2 (saved by Fritzing 0.9.3b)
breadboards: 1

parts:
  YwRobot_Power_Supply1 = YwRobot Breadboard Power Supply [part_number=545043]
  LCD1 = LCD screen
  LCM1602_IIC1 = LCM1602 IIC [part_number="LCM1602 IIC" chip_label="LCM1602 IIC" package="DIP (Dual Inline) [THT]"]
  M1 = ESP-01 Breakout Board Breadboard Adapter [part_number=ESP8266]
  Componente1 = Adafruit ADXL345 [part_number="Adafruit #1231"]

nets:
  VCC: YwRobot_Power_Supply1.VCC#5, YwRobot_Power_Supply1.VCC#6, M1.VCC, Componente1.3.3V, Componente1.CS
  N1: YwRobot_Power_Supply1.VCC#9, YwRobot_Power_Supply1.VCC#10, LCM1602_IIC1.VCC, LCM1602_IIC1.SDA, LCM1602_IIC1.SCL, M1.GP0, M1.GP2, Componente1.SDA/SDIO, Componente1.SCL
  GND: YwRobot_Power_Supply1.GND#11, YwRobot_Power_Supply1.GND#12, M1.GND, Componente1.GND
  N2: YwRobot_Power_Supply1.GND#13, YwRobot_Power_Supply1.GND#14, LCM1602_IIC1.GND
  VSS: LCD1.VSS, LCM1602_IIC1.VSS
  VDD: LCD1.VDD, LCM1602_IIC1.VDD
  N3: LCD1.Contrast, LCM1602_IIC1.V0
  N4: LCD1.RS, LCM1602_IIC1.RS
  N5: LCD1.R/W, LCM1602_IIC1.RW
  N6: LCD1.E, LCM1602_IIC1.E
  N7: LCD1.D0, LCM1602_IIC1.D0
  N8: LCD1.D1, LCM1602_IIC1.D1
  N9: LCD1.D2, LCM1602_IIC1.D2
  N10: LCD1.D3, LCM1602_IIC1.D3
  N11: LCD1.D4, LCM1602_IIC1.D4
  N12: LCD1.D5, LCM1602_IIC1.D5
  N13: LCD1.D6, LCM1602_IIC1.D6
  N14: LCD1.D7, LCM1602_IIC1.D7
  N15: LCD1.Backlight_PWR, LCM1602_IIC1.A
  N16: LCD1.Backlight_(GND), LCM1602_IIC1.K
  N17: LCM1602_IIC1.LED_A, LCM1602_IIC1.LED_B

custom parts:
  YwRobot Breadboard Power Supply: The YwRobot Breadboard Power Supply (MB-V2) has two power rails; they can be 5V or 3V3. Power to the module can be provided through the female USB socket or through the A10 (female) 2.1mm power jack.
  LCD screen: A standard character display, usually with 2x16 characters. Comes in many colors.
  LCM1602 IIC: I2C-Module to use a 1602 or 2004 LCD on with the wire.h libory Serial LCD Modul
  ESP-01 Breakout Board Breadboard Adapter: Generic WiFi Module based on the ESP8266 with onboard PCB antenna and UART communications with breadboard friendly breakout board attached.
  Adafruit ADXL345: Filling out our accelerometer offerings, we now have the really lovely digital ADXL345 from Analog Devices, a triple-axis accelerometer with digital I2C and SPI interface breakout. We added an on-board 3.3V regulator and logic-level shifting circuitry, making it a perfect choice for interfacing with any 3V or 5V microcontroller such as the Arduino. The sensor has three axes of measurements, X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
