# Fritzing sketch NodeMCU+MCP23017 (saved by Fritzing 0.9.3b)
breadboards: 1

parts:
  U1 = NodeMCU V1.0
  IC1 = MCP23017 I2C I/O Expander
  LED1 = smd LED [color="Red (633nm)" package="0805 [SMD]"]
  LED2 = smd LED [color="Red (633nm)" package="0805 [SMD]"]
  LED3 = smd LED [color="Red (633nm)" package="0805 [SMD]"]
  LED4 = smd LED [color="Red (633nm)" package="0805 [SMD]"]
  LED5 = smd LED [color="Yellow (595nm)" package="0805 [SMD]"]
  LED6 = smd LED [color="Yellow (595nm)" package="0805 [SMD]"]
  LED7 = smd LED [color="Yellow (595nm)" package="0805 [SMD]"]
  LED8 = smd LED [color="Green (570nm)" package="0805 [SMD]"]

nets:
  N1: U1.D1, IC1.SCL
  N2: U1.D2, IC1.SDA
  3V3: U1.3V3, IC1.VDD, IC1.RESET
  GND: U1.GND, IC1.VSS, IC1.A0, IC1.A1, IC1.A2, LED1.cathode, LED2.cathode, LED3.cathode, LED4.cathode, LED5.cathode, LED6.cathode, LED7.cathode, LED8.cathode
  N3: IC1.GPA0, LED8.anode
  N4: IC1.GPA1, LED6.anode
  N5: IC1.GPA2, LED7.anode
  N6: IC1.GPA3, LED5.anode
  N7: IC1.GPA4, LED4.anode
  N8: IC1.GPA5, LED3.anode
  N9: IC1.GPA6, LED2.anode
  N10: IC1.GPA7, LED1.anode

custom parts:
  NodeMCU V1.0: ESP8266 based NodeMCU
  MCP23017 I2C I/O Expander: The MCP23017 uses two i2c pins (these can be shared with other i2c devices), and in exchange gives you 16 general purpose pins. You can set each of 16 pins to be input, output, input with a pullup or open drain. There's even the ability to get an interrupt via an external pin when any of the inputs change so you don't have to keep polling the chip.
