# Fritzing sketch SupervisionStation (saved by Fritzing 0.9.3b)
breadboards: 1

parts:
  Raspberry_Pi1 = Raspberry Pi (Model B)
  M1 = ESP-01 Breakout Board Breadboard Adapter [part_number=ESP8266]  # not connected
  LCD2004-I2C1 = LCD2004-I2C
  Componente1 = Arduino Uno (Rev3)

nets:
  5V: Raspberry_Pi1.5V, LCD2004-I2C1.VCC
  N1: Raspberry_Pi1.SDA, Componente1.A4/SDA
  N2: Raspberry_Pi1.SCL, Componente1.A5/SCL
  GND: Raspberry_Pi1.GND, LCD2004-I2C1.GND
  N3: Raspberry_Pi1.TXD, LCD2004-I2C1.TX

custom parts:
  Raspberry Pi (Model B): Raspberry Pi Single-board Computer, Model B
  ESP-01 Breakout Board Breadboard Adapter: Generic WiFi Module based on the ESP8266 with onboard PCB antenna and UART communications with breadboard friendly breakout board attached.
  LCD2004-I2C: A standard character display with 4x20 characters. Comes in many colors with LCM2004 IIC attached.
