# Fritzing sketch SupervisionStation_v2 (saved by Fritzing 0.9.3b)
breadboards: 1

parts:
  M1 = ESP-01 Breakout Board Breadboard Adapter [part_number=ESP8266]  # not connected
  LCD2004-I2C1 = LCD2004-I2C
  Componente1 = Arduino Uno (Rev3)
  YwRobot_Power_Supply1 = YwRobot Breadboard Power Supply [part_number=545043]

nets:
  GND: LCD2004-I2C1.GND, Componente1.GND, YwRobot_Power_Supply1.GND#11, YwRobot_Power_Supply1.GND#12
  VCC: LCD2004-I2C1.VCC, Componente1.5V
  N1: LCD2004-I2C1.RX, Componente1.D3_PWM
  N2: YwRobot_Power_Supply1.VCC#5, YwRobot_Power_Supply1.VCC#6
  N3: YwRobot_Power_Supply1.VCC#9, YwRobot_Power_Supply1.VCC#10
  N4: YwRobot_Power_Supply1.GND#13, YwRobot_Power_Supply1.GND#14

custom parts:
  ESP-01 Breakout Board Breadboard Adapter: Generic WiFi Module based on the ESP8266 with onboard PCB antenna and UART communications with breadboard friendly breakout board attached.
  LCD2004-I2C: A standard character display with 4x20 characters. Comes in many colors with LCM2004 IIC attached.
  YwRobot Breadboard Power Supply: The YwRobot Breadboard Power Supply (MB-V2) has two power rails; they can be 5V or 3V3. Power to the module can be provided through the female USB socket or through the A10 (female) 2.1mm power jack.
